# Fritzing sketch breadboard-layout (saved by Fritzing 0.9.2b)
breadboards: 1

parts:
  R1 = Resistor [tolerance=±5% resistance=500 package=THT]
  R4 = Resistor [tolerance=±5% resistance=500 package=THT]
  R5 = Resistor [tolerance=±5% resistance=500 package=THT]
  R6 = Resistor [tolerance=±5% resistance=500 package=THT]
  R7 = Resistor [tolerance=±5% resistance=500 package=THT]
  R9 = Resistor [tolerance=±5% resistance=100 package=THT]
  R10 = Resistor [tolerance=±5% resistance=100 package=THT]
  R11 = Resistor [tolerance=±5% resistance=100 package=THT]
  R8 = Resistor [tolerance=±5% resistance=100 package=THT]
  Q1 = NPN-Transistor [package="TO92 [THT]"]
  Q5 = NPN-Transistor [package="TO92 [THT]"]
  Q6 = NPN-Transistor [package="TO92 [THT]"]
  Q7 = NPN-Transistor [package="TO92 [THT]"]
  U5 = 7-SEGMENT-4DIGIT [package=7-segment-4digit_longpads_for_pogobed]
  R12 = Resistor [tolerance=±5% resistance=220 package=THT]
  R13 = Resistor [tolerance=±5% resistance=220 package=THT]
  R14 = Resistor [tolerance=±5% resistance=220 package=THT]

nets (from the breadboard view):
  N1: R1.Pin_0, U5.7
  N2: R4.Pin_0, U5.5
  N3: R4.Pin_1, R7.Pin_0
  N4: R5.Pin_0, U5.6, U5.11
  N5: R6.Pin_0, U5.8, U5.9
  N6: R9.Pin_0, R10.Pin_0, R11.Pin_0, R8.Pin_0
  N7: R9.Pin_1, R10.Pin_1, R11.Pin_1, R8.Pin_1
  N8: Q1.E, Q1.C, Q5.E, Q6.E, Q7.E, U5.1, U5.2, U5.3, U5.4, U5.13, U5.14, U5.15, U5.16, R12.Pin_0, R13.Pin_0, R14.Pin_0
  N9: Q1.B, Q5.B, Q6.B, Q7.B
  N10: R12.Pin_1, R13.Pin_1, R14.Pin_1

notes:
  PORTB-0
  PORTB-1
  PORTB-2
  PORTB-3
  A
  TDM LED Lab (rev.1)
